// Logisim project Final.circ as structural Verilog: 7 circuits, main circuit main
module main (
  input  [3:0] PC,
  input  Clear,
  input  in_3,
  input  in_4,
  input  [2:0] in_5,
  output [15:0] Im_Value,
  output [15:0] Alu_Output,
  output Cout,
  output Bout,
  output [15:0] Mult,
  output [15:0] Rem,
  output [5:0] Function,
  output [15:0] Rs,
  output [15:0] Rt
);

  wire clock_1_out, control_unit_1_load, control_unit_1_r_type, control_unit_1_store, or_1_out;
  wire [4:0] multiplexer_1_out, rom_1_rd, rom_1_rs, rom_1_rt, rom_1_shift;
  wire [5:0] rom_1_opcode;
  wire [15:0] i_type_instruction_set_1_im_value, multiplexer_3_out, ram_1_data;

  ROM rom_1 (
    .Inc(PC), .Function(Function), .Shift(rom_1_shift), .Rd(rom_1_rd), .Rt(rom_1_rt), .Rs(rom_1_rs),
    .Opcode(rom_1_opcode));
  I_Type_Instruction_set i_type_instruction_set_1 (
    .Function(Function), .Shift(rom_1_shift), .Rd(rom_1_rd), .Im_Value(i_type_instruction_set_1_im_value));
  Control_Unit control_unit_1 (
    .R_Op1(rom_1_opcode[0]), .R_Op2(rom_1_opcode[1]), .R_Op3(rom_1_opcode[2]), .R_Op4(rom_1_opcode[3]),
    .R_Op5(rom_1_opcode[4]), .R_Op6(rom_1_opcode[5]), .L_Op1(rom_1_opcode[5]), .L_Op2(rom_1_opcode[4]),
    .L_Op3(rom_1_opcode[3]), .L_Op4(rom_1_opcode[2]), .L_Op5(rom_1_opcode[1]), .L_Op6(rom_1_opcode[0]),
    .S_Op1(rom_1_opcode[5]), .S_Op2(rom_1_opcode[4]), .S_Op3(rom_1_opcode[3]), .S_Op4(rom_1_opcode[2]),
    .S_Op5(rom_1_opcode[1]), .S_Op6(rom_1_opcode[1]), .R_type(control_unit_1_r_type),
    .Load(control_unit_1_load), .Store(control_unit_1_store));
  or or_1 (or_1_out, control_unit_1_r_type, control_unit_1_load);
  Multiplexer #(.width(5)) multiplexer_1 (
    .in0(rom_1_rt), .in1(rom_1_rd), .out(multiplexer_1_out), .sel(control_unit_1_r_type));  // open: en
  Registers registers_1 (
    .Write_data(multiplexer_3_out), .Dec_enb(or_1_out), .Rd(multiplexer_1_out), .Clear(Clear), .Rs_Out(Rs),
    .Rs(rom_1_rs), .Rt_Out(Rt), .Rt(rom_1_rt));
  Multiplexer #(.width(16)) multiplexer_2 (
    .in0(Rt), .in1(i_type_instruction_set_1_im_value), .out(Im_Value), .sel(control_unit_1_load));  // open: en
  ALU alu_1 (
    .Rs(Rs), .Rt(Im_Value), .MuxSelect(in_5), .Output(Alu_Output), .Cout(Cout), .Bout(Bout), .Cout_2(Mult),
    .Rem(Rem));
  ALU_Control alu_control_1 (.Sig(control_unit_1_r_type), .Function(Function), .Alu_Control(in_5));
  Clock clock_1 (.out(clock_1_out));
  RAM #(.addrWidth(16), .dataWidth(16), .bus("separate")) ram_1 (
    .addr(Alu_Output), .din(Rt), .data(ram_1_data), .str(control_unit_1_store), .sel(in_3),
    .clk(clock_1_out), .ld(control_unit_1_load), .clr(in_4));
  Multiplexer #(.width(16)) multiplexer_3 (
    .in0(Alu_Output), .in1(ram_1_data), .out(multiplexer_3_out), .sel(control_unit_1_load));  // open: en

  // Notes on the sheet:
  //   Func
  //   SHI
  //   RegWrite
  //   Rt
  //   RegDst
  //   R-Type
  //    RegWrite
  //   Regdst
  //   Aluop1     
  //   Write Data
  //         AluSrc 
  //            MemtoReg
  //               RegWrite
  //        MemRead
  //   AluSrc
  //                          D
  //   MemWrite            
  //   MemtoReg
  //         MemRead 
endmodule

// Reg
module Registers (
  input  [15:0] Write_data,
  input  Dec_enb,
  input  [4:0] Rs,
  input  [4:0] Rd,
  input  Clear,
  input  [4:0] Rt,
  output [15:0] Rs_Out,
  output [15:0] Rt_Out
);

  wire Clock_out, decoder_1_out0, decoder_1_out1, decoder_1_out2, decoder_1_out3, decoder_1_out4,
       decoder_1_out5, decoder_1_out6, decoder_1_out7;
  wire [15:0] register_1_q, register_2_q, register_3_q, register_4_q, register_5_q, register_6_q,
       register_7_q, register_8_q;

  Decoder #(.select(5)) decoder_1 (
    .out0(decoder_1_out0), .out1(decoder_1_out1), .out2(decoder_1_out2), .out3(decoder_1_out3),
    .out4(decoder_1_out4), .out5(decoder_1_out5), .out6(decoder_1_out6), .out7(decoder_1_out7), .sel(Rd),
    .en(Dec_enb));  // open: out8, out9, out10, out11, out12, out13, out14, out15, out16, out17, out18, out19, out20, out21, out22, out23, out24, out25, out26, out27, out28, out29, out30, out31
  Register #(.width(16)) register_1 (
    .D(Write_data), .en(decoder_1_out0), .Q(register_1_q), .clk(Clock_out), .clr(Clear));
  Register #(.width(16)) register_2 (
    .D(Write_data), .en(decoder_1_out1), .Q(register_2_q), .clk(Clock_out), .clr(Clear));
  Register #(.width(16)) register_3 (
    .D(Write_data), .en(decoder_1_out2), .Q(register_3_q), .clk(Clock_out), .clr(Clear));
  Register #(.width(16)) register_4 (
    .D(Write_data), .en(decoder_1_out3), .Q(register_4_q), .clk(Clock_out), .clr(Clear));
  Register #(.width(16)) register_5 (
    .D(Write_data), .en(decoder_1_out4), .Q(register_5_q), .clk(Clock_out), .clr(Clear));
  Register #(.width(16)) register_6 (
    .D(Write_data), .en(decoder_1_out5), .Q(register_6_q), .clk(Clock_out), .clr(Clear));
  Register #(.width(16)) register_7 (
    .D(Write_data), .en(decoder_1_out6), .Q(register_7_q), .clk(Clock_out), .clr(Clear));
  Register #(.width(16)) register_8 (
    .D(Write_data), .en(decoder_1_out7), .Q(register_8_q), .clk(Clock_out), .clr(Clear));
  Clock Clock (.out(Clock_out));
  Multiplexer #(.select(5), .width(16)) multiplexer_1 (
    .in0(register_1_q), .in1(register_2_q), .in2(register_3_q), .in3(register_4_q), .in4(register_5_q),
    .in5(register_6_q), .in6(register_7_q), .in7(register_8_q), .out(Rs_Out), .sel(Rs));  // open: in8, in9, in10, in11, in12, in13, in14, in15, in16, in17, in18, in19, in20, in21, in22, in23, in24, in25, in26, in27, in28, in29, in30, in31, en
  Multiplexer #(.select(5), .width(16)) multiplexer_2 (
    .in0(register_1_q), .in1(register_2_q), .in2(register_3_q), .in3(register_4_q), .in4(register_5_q),
    .in5(register_6_q), .in6(register_7_q), .in7(register_8_q), .out(Rt_Out), .sel(Rt));  // open: in8, in9, in10, in11, in12, in13, in14, in15, in16, in17, in18, in19, in20, in21, in22, in23, in24, in25, in26, in27, in28, in29, in30, in31, en
endmodule

module ALU (
  input  [15:0] Rs,
  input  [15:0] Rt,
  input  [2:0] MuxSelect,
  output [15:0] Output,
  output Cout,
  output Bout,
  output [15:0] Cout_2,
  output [15:0] Rem
);

  wire [15:0] adder_1_out, and_1_out, divider_1_out, multiplier_1_out, not_1_out, or_1_out, subtractor_1_out,
       xor_1_out;

  assign and_1_out = Rs & Rt;  // AND_Gate and_1, 16 bits wide
  assign or_1_out = Rs | Rt;  // OR_Gate or_1, 16 bits wide
  assign xor_1_out = Rs ^ Rt;  // XOR_Gate xor_1, 16 bits wide
  assign not_1_out = ~Rs;  // NOT_Gate not_1, 16 bits wide
  Adder #(.width(16)) adder_1 (.a(Rs), .b(Rt), .out(adder_1_out), .cout(Cout));  // open: cin
  Subtractor #(.width(16)) subtractor_1 (.a(Rs), .b(Rt), .out(subtractor_1_out), .bout(Bout));  // open: bin
  Multiplier #(.width(16)) multiplier_1 (.a(Rs), .b(Rt), .out(multiplier_1_out), .cout(Cout_2));  // open: cin
  Divider #(.width(16)) divider_1 (.a(Rs), .b(Rt), .out(divider_1_out), .rem(Rem));  // open: upper
  Multiplexer #(.select(3), .width(16)) multiplexer_1 (
    .in0(and_1_out), .in1(or_1_out), .in2(xor_1_out), .in3(not_1_out), .in4(adder_1_out),
    .in5(subtractor_1_out), .in6(multiplier_1_out), .in7(divider_1_out), .out(Output), .sel(MuxSelect));  // open: en
endmodule

// CU
module Control_Unit (
  input  R_Op1,
  input  R_Op2,
  input  R_Op3,
  input  R_Op4,
  input  R_Op5,
  input  R_Op6,
  input  L_Op1,
  input  L_Op2,
  input  L_Op3,
  input  L_Op4,
  input  L_Op5,
  input  L_Op6,
  input  S_Op1,
  input  S_Op2,
  input  S_Op3,
  input  S_Op4,
  input  S_Op5,
  input  S_Op6,
  output R_type,
  output Load,
  output Store
);

  wire not_1_out, not_2_out, not_3_out, not_4_out, not_5_out, not_6_out, not_7_out, not_8_out, not_9_out,
       not_10_out, not_11_out;

  not not_1 (not_1_out, R_Op1);
  not not_2 (not_2_out, R_Op2);
  not not_3 (not_3_out, R_Op3);
  not not_4 (not_4_out, R_Op4);
  not not_5 (not_5_out, R_Op5);
  not not_6 (not_6_out, R_Op6);
  not not_7 (not_7_out, L_Op2);
  not not_8 (not_8_out, L_Op3);
  not not_9 (not_9_out, L_Op4);
  not not_10 (not_10_out, S_Op2);
  not not_11 (not_11_out, S_Op4);
  and and_1 (R_type, not_1_out, not_2_out, not_3_out, not_4_out, not_5_out, not_6_out);
  and and_2 (Load, L_Op1, not_7_out, not_8_out, not_9_out, L_Op5, L_Op6);
  and and_3 (Store, S_Op1, not_10_out, S_Op3, not_11_out, S_Op5, S_Op6);
endmodule

// INS_MEM
module ROM (
  input  [3:0] Inc,
  output [5:0] Function,
  output [4:0] Shift,
  output [4:0] Rd,
  output [4:0] Rt,
  output [4:0] Rs,
  output [5:0] Opcode
);

  wire clock_1_out;
  wire [3:0] adder_1_out, register_1_q;

  Clock clock_1 (.out(clock_1_out));
  Adder #(.width(4)) adder_1 (.a(Inc), .b(register_1_q), .out(adder_1_out));  // open: cin, cout
  Register #(.width(4)) register_1 (
    .D(adder_1_out), .en(clock_1_out), .Q(register_1_q), .clk(clock_1_out));  // open: clr
  ROM_part #(.addrWidth(4), .dataWidth(32)) rom_1 (
    .addr(register_1_q), .data({Opcode, Rs, Rt, Rd, Shift, Function}));  // open: sel

  // Notes on the sheet:
  //   contents of rom_1 (hex, n*v repeats v):
  //   210000 220004 210001 220000 ac220002 210000 210202 830004 e30000 8c220003 8c220004 8c220005
endmodule

// A_C
module ALU_Control (
  input  Sig,
  input  [2:0] Alu_Control,
  input  [5:0] Function
);

  and and_1 (Alu_Control[2], Sig, Function[2]);

  assign Function[1:0] = {Alu_Control[0], Alu_Control[1]};
endmodule

// ImVa
module I_Type_Instruction_set (
  input  [5:0] Function,
  input  [4:0] Shift,
  input  [4:0] Rd,
  output [15:0] Im_Value
);


  assign Im_Value = {Rd, Shift, Function};
endmodule
