// Logisim project Project 2.0.circ as structural Verilog: 6 circuits, main circuit main
module main (
  input  [3:0] Inc,
  input  CLR,
  output [15:0] RS_Output,
  output [15:0] RT_Output,
  output [15:0] ALU_Output,
  output Cout,
  output Bout,
  output [15:0] Cout_2,
  output [15:0] Rem
);

  wire CU_regdst;
  wire [2:0] ALU_Control_mux_sel, INS_MEM_function, INS_MEM_opcode;
  wire [3:0] INS_MEM_rd, INS_MEM_rs, INS_MEM_rt;

  ROM INS_MEM (
    .Inc(Inc), .Function(INS_MEM_function), .RD(INS_MEM_rd), .RT(INS_MEM_rt), .RS(INS_MEM_rs),
    .Opcode(INS_MEM_opcode));  // open: Shift
  CU_File CU (.Opcode(INS_MEM_opcode), .RegDst(CU_regdst));  // open: RegWrite, ALUOp
  RegFile RegFile (
    .Write_Data(ALU_Output), .DEC_EN(CU_regdst), .RD(INS_MEM_rd), .Write_Enable(CU_regdst), .CLR(CLR),
    .RS(INS_MEM_rs), .RT(INS_MEM_rt), .RS_Out(RS_Output), .RT_Out(RT_Output));
  ALU_Control ALU_Control (.Aluop(CU_regdst), .Function(INS_MEM_function), .Mux_Sel(ALU_Control_mux_sel));
  ALUFile ALU (
    .RS(RS_Output), .RT(RT_Output), .MuxSelect(ALU_Control_mux_sel), .Output(ALU_Output), .Cout(Cout),
    .Bout(Bout), .Cout_2(Cout_2), .Rem(Rem));
endmodule

module RegFile (
  input  [15:0] Write_Data,
  input  [3:0] RS,
  input  DEC_EN,
  input  [3:0] RD,
  input  [3:0] RT,
  input  Write_Enable,
  input  CLR,
  output [15:0] RS_Out,
  output [15:0] RT_Out
);

  wire and_1_out, and_2_out, and_3_out, and_4_out, and_5_out, and_6_out, and_7_out, and_8_out, CLK_out,
       decoder_1_out0, decoder_1_out1, decoder_1_out2, decoder_1_out3, decoder_1_out4, decoder_1_out5,
       decoder_1_out6, decoder_1_out7;
  wire [15:0] register_1_q, register_2_q, register_3_q, register_4_q, register_5_q, register_6_q,
       register_7_q, register_8_q;

  Decoder #(.select(4)) decoder_1 (
    .out0(decoder_1_out0), .out1(decoder_1_out1), .out2(decoder_1_out2), .out3(decoder_1_out3),
    .out4(decoder_1_out4), .out5(decoder_1_out5), .out6(decoder_1_out6), .out7(decoder_1_out7), .sel(RD),
    .en(DEC_EN));  // open: out8, out9, out10, out11, out12, out13, out14, out15
  and and_1 (and_1_out, decoder_1_out0, Write_Enable);
  and and_2 (and_2_out, decoder_1_out1, Write_Enable);
  and and_3 (and_3_out, decoder_1_out2, Write_Enable);
  and and_4 (and_4_out, decoder_1_out3, Write_Enable);
  and and_5 (and_5_out, decoder_1_out4, Write_Enable);
  and and_6 (and_6_out, decoder_1_out5, Write_Enable);
  and and_7 (and_7_out, decoder_1_out6, Write_Enable);
  and and_8 (and_8_out, decoder_1_out7, Write_Enable);
  Clock CLK (.out(CLK_out));
  Register #(.width(16)) register_1 (.D(Write_Data), .en(and_1_out), .Q(register_1_q), .clk(CLK_out), .clr(CLR));
  Register #(.width(16)) register_2 (.D(Write_Data), .en(and_2_out), .Q(register_2_q), .clk(CLK_out));  // open: clr
  Register #(.width(16)) register_3 (.D(Write_Data), .en(and_3_out), .Q(register_3_q), .clk(CLK_out));  // open: clr
  Register #(.width(16)) register_4 (.D(Write_Data), .en(and_4_out), .Q(register_4_q), .clk(CLK_out));  // open: clr
  Register #(.width(16)) register_5 (.D(Write_Data), .en(and_5_out), .Q(register_5_q), .clk(CLK_out));  // open: clr
  Register #(.width(16)) register_6 (.D(Write_Data), .en(and_6_out), .Q(register_6_q), .clk(CLK_out));  // open: clr
  Register #(.width(16)) register_7 (.D(Write_Data), .en(and_7_out), .Q(register_7_q), .clk(CLK_out));  // open: clr
  Register #(.width(16)) register_8 (.D(Write_Data), .en(and_8_out), .Q(register_8_q), .clk(CLK_out));  // open: clr
  Multiplexer #(.select(4), .width(16)) multiplexer_1 (
    .in0(register_1_q), .in1(register_2_q), .in2(register_3_q), .in3(register_4_q), .in4(register_5_q),
    .in5(register_6_q), .in6(register_7_q), .in7(register_8_q), .out(RS_Out), .sel(RS));  // open: in8, in9, in10, in11, in12, in13, in14, in15, en
  Multiplexer #(.select(4), .width(16)) multiplexer_2 (
    .in0(register_1_q), .in1(register_2_q), .in2(register_3_q), .in3(register_4_q), .in4(register_5_q),
    .in5(register_6_q), .in6(register_7_q), .in7(register_8_q), .out(RT_Out), .sel(RT));  // open: in8, in9, in10, in11, in12, in13, in14, in15, en
endmodule

module ALUFile (
  input  [15:0] RS,
  input  [15:0] RT,
  input  [2:0] MuxSelect,
  output [15:0] Output,
  output Cout,
  output Bout,
  output [15:0] Cout_2,
  output [15:0] Rem
);

  wire [15:0] adder_1_out, and_1_out, divider_1_out, multiplier_1_out, not_1_out, or_1_out, subtractor_1_out,
       xor_1_out;

  assign and_1_out = RS & RT;  // AND_Gate and_1, 16 bits wide
  assign or_1_out = RS | RT;  // OR_Gate or_1, 16 bits wide
  assign xor_1_out = RS ^ RT;  // XOR_Gate xor_1, 16 bits wide
  assign not_1_out = ~RS;  // NOT_Gate not_1, 16 bits wide
  Adder #(.width(16)) adder_1 (.a(RS), .b(RT), .out(adder_1_out), .cout(Cout));  // open: cin
  Subtractor #(.width(16)) subtractor_1 (.a(RS), .b(RT), .out(subtractor_1_out), .bout(Bout));  // open: bin
  Multiplier #(.width(16)) multiplier_1 (.a(RS), .b(RT), .out(multiplier_1_out), .cout(Cout_2));  // open: cin
  Divider #(.width(16)) divider_1 (.a(RS), .b(RT), .out(divider_1_out), .rem(Rem));  // open: upper
  Multiplexer #(.select(3), .width(16)) multiplexer_1 (
    .in0(xor_1_out), .in1(and_1_out), .in2(not_1_out), .in3(or_1_out), .in4(adder_1_out),
    .in5(subtractor_1_out), .in6(multiplier_1_out), .in7(divider_1_out), .out(Output), .sel(MuxSelect));  // open: en
endmodule

module CU_File (
  input  [2:0] Opcode,
  output RegDst,
  output RegWrite,
  output ALUOp
);

  wire not_1_out, not_2_out, not_3_out;

  not not_1 (not_1_out, Opcode[0]);
  not not_2 (not_2_out, Opcode[2]);
  not not_3 (not_3_out, Opcode[1]);
  and R_Type (ALUOp, not_1_out, not_3_out, not_2_out);

  assign RegDst = ALUOp;
  assign RegWrite = ALUOp;
endmodule

module ROM (
  input  [3:0] Inc,
  output [2:0] Function,
  output [1:0] Shift,
  output [3:0] RD,
  output [3:0] RT,
  output [3:0] RS,
  output [2:0] Opcode
);

  wire clock_1_out;
  wire [3:0] adder_1_out, register_1_q;

  Register #(.width(4)) register_1 (.D(adder_1_out), .Q(register_1_q), .clk(clock_1_out));  // open: en, clr
  Clock clock_1 (.out(clock_1_out));
  Adder #(.width(4)) adder_1 (.a(Inc), .b(register_1_q), .out(adder_1_out));  // open: cin, cout
  ROM_part #(.addrWidth(4), .dataWidth(20)) rom_1 (
    .addr(register_1_q), .data({Opcode, RS, RT, RD, Shift, Function}));  // open: sel
endmodule

module ALU_Control (
  input  Aluop,
  input  [2:0] Function,
  output [2:0] Mux_Sel
);

  and and_1 (Mux_Sel[2], Aluop, Function[2]);

  assign Mux_Sel[1:0] = Function[1:0];
endmodule
