// Logisim project Project 2.1.circ as structural Verilog: 8 circuits, main circuit main
module main (
  input  InsCLR,
  input  CLR,
  input  in_3,
  input  [15:0] Test_RegDataIn,
  input  [2:0] Test_RD,
  output [15:0] RS_Output,
  output [2:0] Opcode,
  output [15:0] RT_Output,
  output Cout,
  output Bout,
  output [15:0] ALU_Output,
  output [3:0] Function,
  output [2:0] RS,
  output [2:0] RT,
  output [2:0] RD
);

  wire ALUFile_zero_flag, BrachFile_output_to_mux, clock_1_out, CUFile_alusrc, CUFile_beq_bne, CUFile_branch,
       CUFile_memread, CUFile_memtoreg, CUFile_memwrite, CUFile_regdst, CUFile_regwrite, InsMemCLK_out;
  wire [1:0] CUFile_aluop;
  wire [2:0] multiplexer_2_out;
  wire [3:0] alucontrol_1_alu_select, bit_extender_2_out, rom_1_data;
  wire [10:0] Imdt_value_imdt_value;
  wire [15:0] adder_1_out, adder_2_out, bit_extender_1_out, multiplexer_1_out, multiplexer_4_out, ram_1_data,
       RegFile_rt_output, register_1_q, shifter_1_out;

  Clock InsMemCLK (.out(InsMemCLK_out));
  Register #(.width(16)) register_1 (
    .D(multiplexer_1_out), .Q(register_1_q), .clk(InsMemCLK_out), .clr(InsCLR));  // open: en
  Adder #(.width(16)) adder_1 (.a(16'h1), .b(register_1_q), .out(adder_1_out));  // open: cin, cout
  Multiplexer #(.width(16), .enable("false")) multiplexer_1 (
    .in0(adder_1_out), .in1(adder_2_out), .out(multiplexer_1_out), .sel(BrachFile_output_to_mux));
  ROM #(.addrWidth(16), .dataWidth(20)) rom_1 (
    .addr(register_1_q), .data({Opcode, RS, RT, RD, rom_1_data, Function}));  // open: sel
  CUFile CUFile (
    .Opcode(Opcode), .RegDst(CUFile_regdst), .ALUSrc(CUFile_alusrc), .MemtoReg(CUFile_memtoreg),
    .RegWrite(CUFile_regwrite), .MemRead(CUFile_memread), .MemWrite(CUFile_memwrite), .Branch(CUFile_branch),
    .ALUOp(CUFile_aluop), .BEQ_BNE(CUFile_beq_bne));
  Adder #(.width(16)) adder_2 (.a(adder_1_out), .b(shifter_1_out), .out(adder_2_out));  // open: cin, cout
  Multiplexer #(.width(3), .enable("false")) multiplexer_2 (
    .in0(RT), .in1(RD), .out(multiplexer_2_out), .sel(CUFile_regdst));
  BranchFile BrachFile (
    .Output_to_MUX(BrachFile_output_to_mux), .Beq_Bne_CU_Line_In(CUFile_beq_bne),
    .Branch_CU_Line_In(CUFile_branch), .ALU_Zero_Flag_IN(ALUFile_zero_flag));
  Imdt_value Imdt_value (.Function(Function), .Shift(rom_1_data), .RD(RD), .Imdt_value(Imdt_value_imdt_value));
  RegFile RegFile (
    .Reg_Data_In(multiplexer_4_out), .DEC_EN(1'b1), .RD(multiplexer_2_out), .Write_Enable(CUFile_regwrite),
    .CLR(CLR), .RS_Output(RS_Output), .RS(RS), .RT_Output(RegFile_rt_output), .RT(RT));
  assign bit_extender_1_out = {{5{Imdt_value_imdt_value[10]}}, Imdt_value_imdt_value};  // Bit_Extender bit_extender_1
  Shifter #(.width(16)) shifter_1 (.in(bit_extender_1_out), .\dist (4'b0001), .out(shifter_1_out));
  ALUFile ALUFile (
    .ALU_Data_In_1(RS_Output), .ALU_Data_In_2(RT_Output), .Shift_Selector(bit_extender_2_out), .Cout(Cout),
    .Bout(Bout), .ALU_Output(ALU_Output), .Zero_Flag(ALUFile_zero_flag), .ALU_Select(alucontrol_1_alu_select));
  Multiplexer #(.width(16), .enable("false")) multiplexer_3 (
    .in0(RegFile_rt_output), .in1(bit_extender_1_out), .out(RT_Output), .sel(CUFile_alusrc));
  ALUControl alucontrol_1 (.ALUOp(CUFile_aluop), .Function(Function), .ALU_Select(alucontrol_1_alu_select));
  assign bit_extender_2_out = {{3{1'b1}}, 1'b1};  // Bit_Extender bit_extender_2
  RAM #(.addrWidth(16), .dataWidth(16), .bus("separate")) ram_1 (
    .addr(ALU_Output), .din(RegFile_rt_output), .data(ram_1_data), .str(CUFile_memwrite), .clk(clock_1_out),
    .ld(CUFile_memread), .clr(in_3));  // open: sel
  Clock clock_1 (.out(clock_1_out));
  Multiplexer #(.width(16), .enable("false")) multiplexer_4 (
    .in0(ALU_Output), .in1(ram_1_data), .out(multiplexer_4_out), .sel(CUFile_memtoreg));

  // Notes on the sheet:
  //   contents of rom_1 (hex, n*v repeats v):
  //   0 0 26003 53a07
endmodule

module RegFile (
  input  [15:0] Reg_Data_In,
  input  [2:0] RS,
  input  DEC_EN,
  input  [2:0] RD,
  input  Write_Enable,
  input  [2:0] RT,
  input  CLR,
  output [15:0] RS_Output,
  output [15:0] RT_Output
);

  wire and_1_out, and_2_out, and_3_out, and_4_out, and_5_out, and_6_out, and_7_out, and_8_out, CLK_out,
       decoder_1_out0, decoder_1_out1, decoder_1_out2, decoder_1_out3, decoder_1_out4, decoder_1_out5,
       decoder_1_out6, decoder_1_out7;
  wire [15:0] register_1_q, register_2_q, register_3_q, register_4_q, register_5_q, register_6_q,
       register_7_q, register_8_q;

  Clock CLK (.out(CLK_out));
  Decoder #(.select(3)) decoder_1 (
    .out0(decoder_1_out0), .out1(decoder_1_out1), .out2(decoder_1_out2), .out3(decoder_1_out3),
    .out4(decoder_1_out4), .out5(decoder_1_out5), .out6(decoder_1_out6), .out7(decoder_1_out7), .sel(RD),
    .en(DEC_EN));
  and and_1 (and_1_out, Write_Enable, decoder_1_out0);
  and and_2 (and_2_out, Write_Enable, decoder_1_out1);
  and and_3 (and_3_out, Write_Enable, decoder_1_out2);
  and and_4 (and_4_out, Write_Enable, decoder_1_out3);
  and and_5 (and_5_out, Write_Enable, decoder_1_out4);
  and and_6 (and_6_out, Write_Enable, decoder_1_out5);
  and and_7 (and_7_out, Write_Enable, decoder_1_out6);
  and and_8 (and_8_out, Write_Enable, decoder_1_out7);
  Register #(.width(16)) register_1 (.D(Reg_Data_In), .en(and_1_out), .Q(register_1_q), .clk(CLK_out), .clr(CLR));
  Register #(.width(16)) register_2 (.D(Reg_Data_In), .en(and_2_out), .Q(register_2_q), .clk(CLK_out), .clr(CLR));
  Register #(.width(16)) register_3 (.D(Reg_Data_In), .en(and_3_out), .Q(register_3_q), .clk(CLK_out), .clr(CLR));
  Register #(.width(16)) register_4 (.D(Reg_Data_In), .en(and_4_out), .Q(register_4_q), .clk(CLK_out), .clr(CLR));
  Register #(.width(16)) register_5 (.D(Reg_Data_In), .en(and_5_out), .Q(register_5_q), .clk(CLK_out), .clr(CLR));
  Register #(.width(16)) register_6 (.D(Reg_Data_In), .en(and_6_out), .Q(register_6_q), .clk(CLK_out), .clr(CLR));
  Register #(.width(16)) register_7 (.D(Reg_Data_In), .en(and_7_out), .Q(register_7_q), .clk(CLK_out), .clr(CLR));
  Register #(.width(16)) register_8 (.D(Reg_Data_In), .en(and_8_out), .Q(register_8_q), .clk(CLK_out), .clr(CLR));
  Multiplexer #(.select(3), .width(16)) multiplexer_1 (
    .in0(register_1_q), .in1(register_2_q), .in2(register_3_q), .in3(register_4_q), .in4(register_5_q),
    .in5(register_6_q), .in6(register_7_q), .in7(register_8_q), .out(RS_Output), .sel(RS));  // open: en
  Multiplexer #(.select(3), .width(16)) multiplexer_2 (
    .in0(register_1_q), .in1(register_2_q), .in2(register_3_q), .in3(register_4_q), .in4(register_5_q),
    .in5(register_6_q), .in6(register_7_q), .in7(register_8_q), .out(RT_Output), .sel(RT));  // open: en
endmodule

module ALUFile (
  input  [15:0] ALU_Data_In_1,
  input  [15:0] ALU_Data_In_2,
  input  [3:0] ALU_Select,
  input  [3:0] Shift_Selector,
  output Cout,
  output Bout,
  output [15:0] ALU_Output,
  output Zero_Flag
);

  wire [15:0] adder_1_out, and_1_out, nor_1_out, or_1_out, shifter_1_out, shifter_2_out, subtractor_1_out;

  Adder #(.width(16)) adder_1 (.a(ALU_Data_In_1), .b(ALU_Data_In_2), .out(adder_1_out), .cout(Cout));  // open: cin
  Subtractor #(.width(16)) subtractor_1 (
    .a(ALU_Data_In_1), .b(ALU_Data_In_2), .out(subtractor_1_out), .bout(Bout));  // open: bin
  assign and_1_out = ALU_Data_In_1 & ALU_Data_In_2;  // AND_Gate and_1, 16 bits wide
  assign or_1_out = ALU_Data_In_1 | ALU_Data_In_2;  // OR_Gate or_1, 16 bits wide
  assign nor_1_out = ~(ALU_Data_In_1 | ALU_Data_In_2);  // NOR_Gate nor_1, 16 bits wide
  Shifter #(.width(16)) shifter_1 (.in(ALU_Data_In_1), .\dist (Shift_Selector), .out(shifter_1_out));
  Shifter #(.width(16), .shift("lr")) shifter_2 (.in(ALU_Data_In_1), .\dist (Shift_Selector), .out(shifter_2_out));
  Multiplexer #(.select(4), .width(16)) multiplexer_1 (
    .in1(shifter_2_out), .in2(shifter_1_out), .in3(nor_1_out), .in4(or_1_out), .in5(and_1_out),
    .in6(subtractor_1_out), .in7(adder_1_out), .out(ALU_Output), .sel(ALU_Select));  // open: in0, in8, in9, in10, in11, in12, in13, in14, in15, en
  or or_2 (Zero_Flag, ALU_Output[0], ALU_Output[1], ALU_Output[2], ALU_Output[3], ALU_Output[4], ALU_Output[5], ALU_Output[6], ALU_Output[7], ALU_Output[8], ALU_Output[9], ALU_Output[10], ALU_Output[11], ALU_Output[12], ALU_Output[13], ALU_Output[14], ALU_Output[15]);
endmodule

module CUFile (
  input  [2:0] Opcode,
  output RegDst,
  output ALUSrc,
  output MemtoReg,
  output RegWrite,
  output MemRead,
  output MemWrite,
  output Branch,
  output [1:0] ALUOp,
  output BEQ_BNE
);

  wire not_1_out, not_2_out, not_3_out, not_4_out, not_5_out, not_6_out, not_7_out, not_8_out;

  not not_1 (not_1_out, Opcode[2]);
  not not_2 (not_2_out, Opcode[1]);
  not not_3 (not_3_out, Opcode[0]);
  and R_type (ALUOp[1], not_1_out, not_2_out, not_3_out);
  not not_4 (not_4_out, Opcode[2]);
  and lw (MemRead, not_4_out, Opcode[1], not_6_out);
  not not_5 (not_5_out, Opcode[2]);
  not not_6 (not_6_out, Opcode[0]);
  not not_7 (not_7_out, Opcode[1]);
  and sw (MemWrite, not_5_out, not_7_out, Opcode[0]);
  not not_8 (not_8_out, Opcode[2]);
  and beq (ALUOp[0], not_8_out, Opcode[1], Opcode[0]);
  and bne (BEQ_BNE, Opcode[2], Opcode[1], Opcode[0]);
  or or_1 (ALUSrc, MemRead, MemWrite);
  or or_2 (RegWrite, ALUOp[1], MemRead);

  assign Branch = ALUOp[0];
  assign MemtoReg = MemRead;
  assign RegDst = ALUOp[1];
endmodule

module IntructionMem (
  input  [3:0] PC,
  output [3:0] Function,
  output [3:0] Shift,
  output [2:0] RD,
  output [2:0] RT,
  output [2:0] RS,
  output [2:0] Opcode
);

  wire InsMemCLK_out;
  wire [3:0] adder_1_out, register_1_q;

  Clock InsMemCLK (.out(InsMemCLK_out));
  Register #(.width(4)) register_1 (.D(adder_1_out), .Q(register_1_q), .clk(InsMemCLK_out));  // open: en, clr
  Adder #(.width(4)) adder_1 (.a(PC), .b(register_1_q), .out(adder_1_out));  // open: cin, cout
  ROM #(.addrWidth(4), .dataWidth(20)) rom_1 (
    .addr(register_1_q), .data({Opcode, RS, RT, RD, Shift, Function}));  // open: sel

  // Notes on the sheet:
  //   contents of rom_1 (hex, n*v repeats v):
  //   27a07 47a07 47207 4c07 4a84b 26003
endmodule

module ALUControl (
  input  [1:0] ALUOp,
  input  [3:0] Function,
  output [3:0] ALU_Select
);

  and and_1 (ALU_Select[3], ALUOp[0], Function[3]);

  assign ALU_Select[2:0] = Function[2:0];
endmodule

module Imdt_value (
  input  [3:0] Function,
  input  [3:0] Shift,
  input  [2:0] RD,
  output [10:0] Imdt_value
);


  assign Imdt_value = {RD, Shift, Function};
endmodule

module BranchFile (
  input  Beq_Bne_CU_Line_In,
  input  Branch_CU_Line_In,
  input  ALU_Zero_Flag_IN,
  output Output_to_MUX
);

  wire not_1_out, xor_1_out;

  and and_1 (Output_to_MUX, Beq_Bne_CU_Line_In, not_1_out);
  not not_1 (not_1_out, xor_1_out);
  xor xor_1 (xor_1_out, Branch_CU_Line_In, ALU_Zero_Flag_IN);
endmodule
